// Logisim project 22-bit-ALU.circ as structural Verilog: 13 circuits, main circuit main
module main (
  input  [1:0] Control,
  input  [21:0] A,
  input  [21:0] B,
  output [21:0] Result,
  output Zero,
  output Negative,
  output Overflow,
  output Carry
);

  _22_bit_ALU u_22_bit_alu_1 (
    .A(A), .B(B), .Result(Result), .Zero(Zero), .Negative(Negative), .Overflow(Overflow), .Carry(Carry),
    .Control0(Control[0]), .Control1(Control[1]));
endmodule

// 22-bit AND
module _22_bit_and (
  input  [21:0] A,
  input  [21:0] B,
  output [21:0] Result
);

  assign Result = A & B;  // AND_Gate and_1, 22 bits wide
endmodule

// 22-bit OR
module _22_bit_OR (
  input  [21:0] A,
  input  [21:0] B,
  output [21:0] Result
);

  assign Result = A | B;  // OR_Gate or_1, 22 bits wide
endmodule

module Full_adder (
  input  Carry_in,
  input  A,
  input  B,
  output Result,
  output Carry_out
);

  wire and_1_out, and_2_out, xor_1_out;

  and and_1 (and_1_out, B, A);
  xor xor_1 (xor_1_out, A, B);
  or or_1 (Carry_out, and_1_out, and_2_out);
  and and_2 (and_2_out, xor_1_out, Carry_in);
  xor xor_2 (Result, Carry_in, xor_1_out);
endmodule

module _22_bit_full_adder (
  input  Carry_in,
  input  A0,
  input  B0,
  input  A1,
  input  B1,
  input  A2,
  input  B2,
  input  A3,
  input  B3,
  input  A4,
  input  B4,
  input  A5,
  input  B5,
  input  A6,
  input  B6,
  input  A7,
  input  B7,
  input  A8,
  input  B8,
  input  A9,
  input  B9,
  input  A10,
  input  B10,
  input  A11,
  input  B11,
  input  A12,
  input  B12,
  input  A13,
  input  B13,
  input  A14,
  input  B14,
  input  A15,
  input  B15,
  input  A16,
  input  B16,
  input  A17,
  input  B17,
  input  A18,
  input  B18,
  input  A19,
  input  B19,
  input  A20,
  input  B20,
  input  A21,
  input  B21,
  output Result0,
  output Result1,
  output Result2,
  output Result3,
  output Result4,
  output Result5,
  output Result6,
  output Result7,
  output Result8,
  output Result9,
  output Result10,
  output Result11,
  output Result12,
  output Result13,
  output Result14,
  output Result15,
  output Result16,
  output Result17,
  output Result18,
  output Result19,
  output Result20,
  output Result21,
  output Carry
);

  wire full_adder_1_carry_out, full_adder_2_carry_out, full_adder_3_carry_out, full_adder_4_carry_out,
       full_adder_5_carry_out, full_adder_6_carry_out, full_adder_7_carry_out, full_adder_8_carry_out,
       full_adder_9_carry_out, full_adder_10_carry_out, full_adder_11_carry_out, full_adder_12_carry_out,
       full_adder_13_carry_out, full_adder_14_carry_out, full_adder_15_carry_out, full_adder_16_carry_out,
       full_adder_17_carry_out, full_adder_18_carry_out, full_adder_19_carry_out, full_adder_20_carry_out,
       full_adder_21_carry_out;

  Full_adder full_adder_1 (.Carry_in(Carry_in), .A(A0), .B(B0), .Result(Result0), .Carry_out(full_adder_1_carry_out));
  Full_adder full_adder_2 (
    .Carry_in(full_adder_1_carry_out), .A(A1), .B(B1), .Result(Result1), .Carry_out(full_adder_2_carry_out));
  Full_adder full_adder_3 (
    .Carry_in(full_adder_2_carry_out), .A(A2), .B(B2), .Result(Result2), .Carry_out(full_adder_3_carry_out));
  Full_adder full_adder_4 (
    .Carry_in(full_adder_3_carry_out), .A(A3), .B(B3), .Result(Result3), .Carry_out(full_adder_4_carry_out));
  Full_adder full_adder_5 (
    .Carry_in(full_adder_4_carry_out), .A(A4), .B(B4), .Result(Result4), .Carry_out(full_adder_5_carry_out));
  Full_adder full_adder_6 (
    .Carry_in(full_adder_5_carry_out), .A(A5), .B(B5), .Result(Result5), .Carry_out(full_adder_6_carry_out));
  Full_adder full_adder_7 (
    .Carry_in(full_adder_6_carry_out), .A(A6), .B(B6), .Result(Result6), .Carry_out(full_adder_7_carry_out));
  Full_adder full_adder_8 (
    .Carry_in(full_adder_7_carry_out), .A(A7), .B(B7), .Result(Result7), .Carry_out(full_adder_8_carry_out));
  Full_adder full_adder_9 (
    .Carry_in(full_adder_8_carry_out), .A(A8), .B(B8), .Result(Result8), .Carry_out(full_adder_9_carry_out));
  Full_adder full_adder_10 (
    .Carry_in(full_adder_9_carry_out), .A(A9), .B(B9), .Result(Result9), .Carry_out(full_adder_10_carry_out));
  Full_adder full_adder_11 (
    .Carry_in(full_adder_10_carry_out), .A(A10), .B(B10), .Result(Result10),
    .Carry_out(full_adder_11_carry_out));
  Full_adder full_adder_12 (
    .Carry_in(full_adder_11_carry_out), .A(A11), .B(B11), .Result(Result11),
    .Carry_out(full_adder_12_carry_out));
  Full_adder full_adder_13 (
    .Carry_in(full_adder_12_carry_out), .A(A12), .B(B12), .Result(Result12),
    .Carry_out(full_adder_13_carry_out));
  Full_adder full_adder_14 (
    .Carry_in(full_adder_13_carry_out), .A(A13), .B(B13), .Result(Result13),
    .Carry_out(full_adder_14_carry_out));
  Full_adder full_adder_15 (
    .Carry_in(full_adder_14_carry_out), .A(A14), .B(B14), .Result(Result14),
    .Carry_out(full_adder_15_carry_out));
  Full_adder full_adder_16 (
    .Carry_in(full_adder_15_carry_out), .A(A15), .B(B15), .Result(Result15),
    .Carry_out(full_adder_16_carry_out));
  Full_adder full_adder_17 (
    .Carry_in(full_adder_16_carry_out), .A(A16), .B(B16), .Result(Result16),
    .Carry_out(full_adder_17_carry_out));
  Full_adder full_adder_18 (
    .Carry_in(full_adder_17_carry_out), .A(A17), .B(B17), .Result(Result17),
    .Carry_out(full_adder_18_carry_out));
  Full_adder full_adder_19 (
    .Carry_in(full_adder_18_carry_out), .A(A18), .B(B18), .Result(Result18),
    .Carry_out(full_adder_19_carry_out));
  Full_adder full_adder_20 (
    .Carry_in(full_adder_19_carry_out), .A(A19), .B(B19), .Result(Result19),
    .Carry_out(full_adder_20_carry_out));
  Full_adder full_adder_21 (
    .Carry_in(full_adder_20_carry_out), .A(A20), .B(B20), .Result(Result20),
    .Carry_out(full_adder_21_carry_out));
  Full_adder full_adder_22 (.Carry_in(full_adder_21_carry_out), .A(A21), .B(B21), .Result(Result21), .Carry_out(Carry));
endmodule

// FA
module _22_bit_full_adder_concise (
  input  Carry_in,
  input  [21:0] A,
  input  [21:0] B,
  output [21:0] Result,
  output Carry
);

  wire full_adder_1_carry_out, full_adder_2_carry_out, full_adder_3_carry_out, full_adder_4_carry_out,
       full_adder_5_carry_out, full_adder_6_carry_out, full_adder_7_carry_out, full_adder_8_carry_out,
       full_adder_9_carry_out, full_adder_10_carry_out, full_adder_11_carry_out, full_adder_12_carry_out,
       full_adder_13_carry_out, full_adder_14_carry_out, full_adder_15_carry_out, full_adder_16_carry_out,
       full_adder_17_carry_out, full_adder_18_carry_out, full_adder_19_carry_out, full_adder_20_carry_out,
       full_adder_21_carry_out;

  Full_adder full_adder_1 (
    .Carry_in(Carry_in), .A(A[0]), .B(B[0]), .Result(Result[0]), .Carry_out(full_adder_1_carry_out));
  Full_adder full_adder_2 (
    .Carry_in(full_adder_1_carry_out), .A(A[1]), .B(B[1]), .Result(Result[1]),
    .Carry_out(full_adder_2_carry_out));
  Full_adder full_adder_3 (
    .Carry_in(full_adder_2_carry_out), .A(A[2]), .B(B[2]), .Result(Result[2]),
    .Carry_out(full_adder_3_carry_out));
  Full_adder full_adder_4 (
    .Carry_in(full_adder_3_carry_out), .A(A[3]), .B(B[3]), .Result(Result[3]),
    .Carry_out(full_adder_4_carry_out));
  Full_adder full_adder_5 (
    .Carry_in(full_adder_4_carry_out), .A(A[4]), .B(B[4]), .Result(Result[4]),
    .Carry_out(full_adder_5_carry_out));
  Full_adder full_adder_6 (
    .Carry_in(full_adder_5_carry_out), .A(A[5]), .B(B[5]), .Result(Result[5]),
    .Carry_out(full_adder_6_carry_out));
  Full_adder full_adder_7 (
    .Carry_in(full_adder_6_carry_out), .A(A[6]), .B(B[6]), .Result(Result[6]),
    .Carry_out(full_adder_7_carry_out));
  Full_adder full_adder_8 (
    .Carry_in(full_adder_7_carry_out), .A(A[7]), .B(B[7]), .Result(Result[7]),
    .Carry_out(full_adder_8_carry_out));
  Full_adder full_adder_9 (
    .Carry_in(full_adder_8_carry_out), .A(A[8]), .B(B[8]), .Result(Result[8]),
    .Carry_out(full_adder_9_carry_out));
  Full_adder full_adder_10 (
    .Carry_in(full_adder_9_carry_out), .A(A[9]), .B(B[9]), .Result(Result[9]),
    .Carry_out(full_adder_10_carry_out));
  Full_adder full_adder_11 (
    .Carry_in(full_adder_10_carry_out), .A(A[10]), .B(B[10]), .Result(Result[10]),
    .Carry_out(full_adder_11_carry_out));
  Full_adder full_adder_12 (
    .Carry_in(full_adder_11_carry_out), .A(A[11]), .B(B[11]), .Result(Result[11]),
    .Carry_out(full_adder_12_carry_out));
  Full_adder full_adder_13 (
    .Carry_in(full_adder_12_carry_out), .A(A[12]), .B(B[12]), .Result(Result[12]),
    .Carry_out(full_adder_13_carry_out));
  Full_adder full_adder_14 (
    .Carry_in(full_adder_13_carry_out), .A(A[13]), .B(B[13]), .Result(Result[13]),
    .Carry_out(full_adder_14_carry_out));
  Full_adder full_adder_15 (
    .Carry_in(full_adder_14_carry_out), .A(A[14]), .B(B[14]), .Result(Result[14]),
    .Carry_out(full_adder_15_carry_out));
  Full_adder full_adder_16 (
    .Carry_in(full_adder_15_carry_out), .A(A[15]), .B(B[15]), .Result(Result[15]),
    .Carry_out(full_adder_16_carry_out));
  Full_adder full_adder_17 (
    .Carry_in(full_adder_16_carry_out), .A(A[16]), .B(B[16]), .Result(Result[16]),
    .Carry_out(full_adder_17_carry_out));
  Full_adder full_adder_18 (
    .Carry_in(full_adder_17_carry_out), .A(A[17]), .B(B[17]), .Result(Result[17]),
    .Carry_out(full_adder_18_carry_out));
  Full_adder full_adder_19 (
    .Carry_in(full_adder_18_carry_out), .A(A[18]), .B(B[18]), .Result(Result[18]),
    .Carry_out(full_adder_19_carry_out));
  Full_adder full_adder_20 (
    .Carry_in(full_adder_19_carry_out), .A(A[19]), .B(B[19]), .Result(Result[19]),
    .Carry_out(full_adder_20_carry_out));
  Full_adder full_adder_21 (
    .Carry_in(full_adder_20_carry_out), .A(A[20]), .B(B[20]), .Result(Result[20]),
    .Carry_out(full_adder_21_carry_out));
  Full_adder full_adder_22 (
    .Carry_in(full_adder_21_carry_out), .A(A[21]), .B(B[21]), .Result(Result[21]), .Carry_out(Carry));
endmodule

module _22_bit_xor (
  input  Control,
  input  [21:0] B,
  output [21:0] Result
);

  wire [21:0] bit_extender_1_out;

  assign bit_extender_1_out = {{21{Control}}, Control};  // Bit_Extender bit_extender_1
  assign Result = bit_extender_1_out ^ B;  // XOR_Gate xor_1, 22 bits wide
endmodule

// 32-bit \nADD/SUB
module Add_sub (
  input  Sub,
  input  [21:0] A,
  input  [21:0] B,
  output [21:0] Result,
  output Carry,
  output Overflow
);

  wire and_1_out, and_2_out, n21th_bit_out_1__21th_bit, n21th_bit_out_2__21th_bit, n21th_bit_out_3__21th_bit,
       not_1_out, not_2_out, not_3_out;
  wire [21:0] n22_bit_xor_1_result;

  _21th_bit_out u_21th_bit_out_1 (.Input(A), ._21th_bit(n21th_bit_out_1__21th_bit));
  not not_1 (not_1_out, n21th_bit_out_1__21th_bit);
  _21th_bit_out u_21th_bit_out_2 (.Input(B), ._21th_bit(n21th_bit_out_2__21th_bit));
  not not_2 (not_2_out, n21th_bit_out_2__21th_bit);
  _22_bit_xor u_22_bit_xor_1 (.B(B), .Result(n22_bit_xor_1_result), .Control(Sub));
  _22_bit_full_adder_concise u_22_bit_full_adder_concise_1 (
    .A(A), .B(n22_bit_xor_1_result), .Result(Result), .Carry_in(Sub), .Carry(Carry));
  _21th_bit_out u_21th_bit_out_3 (.Input(Result), ._21th_bit(n21th_bit_out_3__21th_bit));
  not not_3 (not_3_out, n21th_bit_out_3__21th_bit);
  and and_1 (and_1_out, not_3_out, n21th_bit_out_2__21th_bit, n21th_bit_out_1__21th_bit);
  and and_2 (and_2_out, n21th_bit_out_3__21th_bit, not_2_out, not_1_out);
  or or_1 (Overflow, and_1_out, and_2_out);

  // Notes on the sheet:
  //   A21
  //   B21
  //   Result 21
endmodule

// 21th
module _21th_bit_out (
  input  [21:0] Input,
  output _21th_bit
);


  assign _21th_bit = Input[21];
endmodule

// Reduce-OR
module _22_bit_reduce_or (
  input  [21:0] Input,
  output Output
);

  or or_1 (Output, Input[10], Input[0], Input[1], Input[2], Input[3], Input[4], Input[5], Input[6], Input[7], Input[8], Input[9], Input[11], Input[12], Input[13], Input[14], Input[15], Input[16], Input[17], Input[18], Input[19], Input[20], Input[21]);
endmodule

module _22_bit_ALU (
  input  [21:0] A,
  input  Control0,
  input  Control1,
  input  [21:0] B,
  output [21:0] Result,
  output Zero,
  output Negative,
  output Overflow,
  output Carry
);

  wire n22_bit_reduce_or_1_output;
  wire [21:0] add_sub_1_result, multiplexer_1_out, n22_bitwise_and_1__0, n22_bitwise_or_1__0;

  _22_bitwise_and u_22_bitwise_and_1 (
    .A0(A[0]), .B0(B[0]), .A1(A[1]), .B1(B[1]), .A2(A[2]), .B2(B[2]), .A3(A[3]), .B3(B[3]), .A4(A[4]),
    .B4(B[4]), .A5(A[5]), .B5(B[5]), .A6(A[6]), .B6(B[6]), .A7(A[7]), .B7(B[7]), .A8(A[8]), .B8(B[8]),
    .A9(A[9]), .B9(B[9]), .A10(A[10]), .B10(B[10]), .A11(A[11]), .B11(B[11]), .A12(A[12]), .B12(B[12]),
    .A13(A[13]), .B13(B[13]), .A14(A[14]), .B14(B[14]), .A15(A[15]), .B15(B[15]), .A16(A[16]), .B16(B[16]),
    .A17(A[17]), .B17(B[17]), .A18(A[18]), .B18(B[18]), .A19(A[19]), .B19(B[19]), .A20(A[20]), .B20(B[20]),
    .A21(A[21]), .B21(B[21]), ._0(n22_bitwise_and_1__0[0]), ._1(n22_bitwise_and_1__0[1]),
    ._2(n22_bitwise_and_1__0[2]), ._3(n22_bitwise_and_1__0[3]), ._4(n22_bitwise_and_1__0[4]),
    ._5(n22_bitwise_and_1__0[5]), ._6(n22_bitwise_and_1__0[6]), ._7(n22_bitwise_and_1__0[7]),
    ._8(n22_bitwise_and_1__0[8]), ._9(n22_bitwise_and_1__0[9]), ._10(n22_bitwise_and_1__0[10]),
    ._11(n22_bitwise_and_1__0[11]), ._12(n22_bitwise_and_1__0[12]), ._13(n22_bitwise_and_1__0[13]),
    ._14(n22_bitwise_and_1__0[14]), ._15(n22_bitwise_and_1__0[15]), ._16(n22_bitwise_and_1__0[16]),
    ._17(n22_bitwise_and_1__0[17]), ._18(n22_bitwise_and_1__0[18]), ._19(n22_bitwise_and_1__0[19]),
    ._20(n22_bitwise_and_1__0[20]), ._21(n22_bitwise_and_1__0[21]));
  _22_bitwise_or u_22_bitwise_or_1 (
    .A0(A[0]), .B0(B[0]), .A1(A[1]), .B1(B[1]), .A2(A[2]), .B2(B[2]), .A3(A[3]), .B3(B[3]), .A4(A[4]),
    .B4(B[4]), .A5(A[5]), .B5(B[5]), .A6(A[6]), .B6(B[6]), .A7(A[7]), .B7(B[7]), .A8(A[8]), .B8(B[8]),
    .A9(A[9]), .B9(B[9]), .A10(A[10]), .B10(B[10]), .A11(A[11]), .B11(B[11]), .A12(A[12]), .B12(B[12]),
    .A13(A[13]), .B13(B[13]), .A14(A[14]), .B14(B[14]), .A15(A[15]), .B15(B[15]), .A16(A[16]), .B16(B[16]),
    .A17(A[17]), .B17(B[17]), .A18(A[18]), .B18(B[18]), .A19(A[19]), .B19(B[19]), .A20(A[20]), .B20(B[20]),
    .A21(A[21]), .B21(B[21]), ._0(n22_bitwise_or_1__0[0]), ._1(n22_bitwise_or_1__0[1]),
    ._2(n22_bitwise_or_1__0[2]), ._3(n22_bitwise_or_1__0[3]), ._4(n22_bitwise_or_1__0[4]),
    ._5(n22_bitwise_or_1__0[5]), ._6(n22_bitwise_or_1__0[6]), ._7(n22_bitwise_or_1__0[7]),
    ._8(n22_bitwise_or_1__0[8]), ._9(n22_bitwise_or_1__0[9]), ._10(n22_bitwise_or_1__0[10]),
    ._11(n22_bitwise_or_1__0[11]), ._12(n22_bitwise_or_1__0[12]), ._13(n22_bitwise_or_1__0[13]),
    ._14(n22_bitwise_or_1__0[14]), ._15(n22_bitwise_or_1__0[15]), ._16(n22_bitwise_or_1__0[16]),
    ._17(n22_bitwise_or_1__0[17]), ._18(n22_bitwise_or_1__0[18]), ._19(n22_bitwise_or_1__0[19]),
    ._20(n22_bitwise_or_1__0[20]), ._21(n22_bitwise_or_1__0[21]));
  Add_sub add_sub_1 (.Sub(Control0), .A(A), .B(B), .Result(add_sub_1_result), .Carry(Carry), .Overflow(Overflow));
  Multiplexer #(.width(22), .enable("false")) multiplexer_1 (
    .in0(n22_bitwise_and_1__0), .in1(n22_bitwise_or_1__0), .out(multiplexer_1_out), .sel(Control0));
  Multiplexer #(.width(22), .enable("false")) multiplexer_2 (
    .in0(multiplexer_1_out), .in1(add_sub_1_result), .out(Result), .sel(Control1));
  _21th_bit_out u_21th_bit_out_1 (.Input(Result), ._21th_bit(Negative));
  _22_bit_reduce_or u_22_bit_reduce_or_1 (.Input(Result), .Output(n22_bit_reduce_or_1_output));
  not not_1 (Zero, n22_bit_reduce_or_1_output);
endmodule

module _22_bitwise_and (
  input  A0,
  input  B0,
  input  A1,
  input  B1,
  input  A2,
  input  B2,
  input  A3,
  input  B3,
  input  A4,
  input  B4,
  input  A5,
  input  B5,
  input  A6,
  input  B6,
  input  A7,
  input  B7,
  input  A8,
  input  B8,
  input  A9,
  input  B9,
  input  A10,
  input  B10,
  input  A11,
  input  B11,
  input  A12,
  input  B12,
  input  A13,
  input  B13,
  input  A14,
  input  B14,
  input  A15,
  input  B15,
  input  A16,
  input  B16,
  input  A17,
  input  B17,
  input  A18,
  input  B18,
  input  A19,
  input  B19,
  input  A20,
  input  B20,
  input  A21,
  input  B21,
  output _0,
  output _1,
  output _2,
  output _3,
  output _4,
  output _5,
  output _6,
  output _7,
  output _8,
  output _9,
  output _10,
  output _11,
  output _12,
  output _13,
  output _14,
  output _15,
  output _16,
  output _17,
  output _18,
  output _19,
  output _20,
  output _21
);

  and and_1 (_0, A0, B0);
  and and_2 (_1, A1, B1);
  and and_3 (_2, A2, B2);
  and and_4 (_3, A3, B3);
  and and_5 (_4, A4, B4);
  and and_6 (_5, A5, B5);
  and and_7 (_6, A6, B6);
  and and_8 (_7, A7, B7);
  and and_9 (_8, A8, B8);
  and and_10 (_9, A9, B9);
  and and_11 (_10, A10, B10);
  and and_12 (_11, A11, B11);
  and and_13 (_12, A12, B12);
  and and_14 (_13, A13, B13);
  and and_15 (_14, A14, B14);
  and and_16 (_15, A15, B15);
  and and_17 (_16, A16, B16);
  and and_18 (_17, A17, B17);
  and and_19 (_18, A18, B18);
  and and_20 (_19, A19, B19);
  and and_21 (_20, A20, B20);
  and and_22 (_21, A21, B21);
endmodule

module _22_bitwise_or (
  input  A0,
  input  B0,
  input  A1,
  input  B1,
  input  A2,
  input  B2,
  input  A3,
  input  B3,
  input  A4,
  input  B4,
  input  A5,
  input  B5,
  input  A6,
  input  B6,
  input  A7,
  input  B7,
  input  A8,
  input  B8,
  input  A9,
  input  B9,
  input  A10,
  input  B10,
  input  A11,
  input  B11,
  input  A12,
  input  B12,
  input  A13,
  input  B13,
  input  A14,
  input  B14,
  input  A15,
  input  B15,
  input  A16,
  input  B16,
  input  A17,
  input  B17,
  input  A18,
  input  B18,
  input  A19,
  input  B19,
  input  A20,
  input  B20,
  input  A21,
  input  B21,
  output _0,
  output _1,
  output _2,
  output _3,
  output _4,
  output _5,
  output _6,
  output _7,
  output _8,
  output _9,
  output _10,
  output _11,
  output _12,
  output _13,
  output _14,
  output _15,
  output _16,
  output _17,
  output _18,
  output _19,
  output _20,
  output _21
);

  or or_1 (_0, A0, B0);
  or or_2 (_1, A1, B1);
  or or_3 (_2, A2, B2);
  or or_4 (_3, A3, B3);
  or or_5 (_4, A4, B4);
  or or_6 (_5, A5, B5);
  or or_7 (_6, A6, B6);
  or or_8 (_7, A7, B7);
  or or_9 (_8, A8, B8);
  or or_10 (_9, A9, B9);
  or or_11 (_10, A10, B10);
  or or_12 (_11, A11, B11);
  or or_13 (_12, A12, B12);
  or or_14 (_13, A13, B13);
  or or_15 (_14, A14, B14);
  or or_16 (_15, A15, B15);
  or or_17 (_16, A16, B16);
  or or_18 (_17, A17, B17);
  or or_19 (_18, A18, B18);
  or or_20 (_19, A19, B19);
  or or_21 (_20, A20, B20);
  or or_22 (_21, A21, B21);
endmodule
