// Logisim project main.circ as structural Verilog
module main (
  input  Reset
);

  wire clock_1_out, cpu_1_memread, cpu_1_memwrite;
  wire [10:0] cpu_1_memaddress;
  wire [21:0] cpu_1_mem_dataout, ram_1_data;

  Clock clock_1 (.out(clock_1_out));
  // AND_Gate and_1 is placed but not wired
  // NOT_Gate not_1 is placed but not wired
  CPU cpu_1 (
    .clock(clock_1_out), .Reset(Reset), .Mem_DataOut(cpu_1_mem_dataout), .MemRead(cpu_1_memread),
    .MemWrite(cpu_1_memwrite), .Mem_DataIN(ram_1_data), .MemAddress(cpu_1_memaddress));  // open: HLT
  // Probe on ram_1_data
  RAM #(.addrWidth(11), .dataWidth(22), .bus("separate")) ram_1 (
    .addr(cpu_1_memaddress), .din(cpu_1_mem_dataout), .data(ram_1_data), .str(cpu_1_memwrite), .sel(1'b1),
    .clk(clock_1_out), .ld(1'b1), .clr(1'b0));
endmodule

module CU (
  input  reset,
  input  clock,
  input  [4:0] Opcode_In,
  output [10:0] AD,
  output [3:0] F,
  output Mem_RD,
  output Mem_WR,
  output HLT
);

  wire [1:0] rom_1_data;
  wire [5:0] BR_01, BR_11, CAR_q, multiplexer_1_out;
  wire [6:6] adder_2_out;
  wire [17:13] rom_1_data_2;

  Register #(.width(6)) CAR (.D(multiplexer_1_out), .en(1'b1), .Q(CAR_q), .clk(clock), .clr(reset));
  Adder #(.width(6)) adder_1 (.a(CAR_q), .b(6'b000001), .out(BR_01), .cin(1'b0));  // open: cout
  Adder #(.width(7)) adder_2 (
    .a({Opcode_In, 2'b00}), .b(7'b0000011), .out({adder_2_out[6], BR_11}), .cin(1'b0));  // open: cout
  Multiplexer #(.select(2), .width(6), .enable("false")) multiplexer_1 (
    .in0({6{1'b0}}), .in1(BR_01), .in2(AD[5:0]), .in3(BR_11), .out(multiplexer_1_out), .sel(rom_1_data));
  ROM #(.addrWidth(6), .dataWidth(22)) rom_1 (.addr(CAR_q), .data({F, rom_1_data_2, rom_1_data, AD}), .sel(1'b1));
  Comparator #(.width(4)) comparator_1 (.a(F), .b(4'b0011), .eq(Mem_RD));  // open: gt, lt
  Comparator #(.width(4)) comparator_2 (.a(F), .b(4'b1011), .eq(Mem_WR));  // open: gt, lt
  Comparator #(.width(4)) comparator_3 (.a(F), .b(4'b1111), .eq(HLT));  // open: gt, lt

  // Other names for the same wires on the sheet: unused[4:0] = AD[10:6]

  // Notes on the sheet:
  //   contents of rom_1 (hex, n*v repeats v):
  //   40800 c0800 81800 140800 c0800 180800 0 140800 c0800 1c0800 0 140800 280800 2c0800 0 140800 c0800
  //   200800 0 140800 c0800 240800 0 300800 0 0 0 100800 0 0 0 140800 c0800 300800 0 140800 c0800 340800
  //   25*0 3c0000
endmodule

module CPU (
  input  [21:0] Mem_DataIN,
  input  clock,
  input  Reset,
  output [21:0] Mem_DataOut,
  output [10:0] MemAddress,
  output MemRead,
  output MemWrite,
  output HLT
);

  wire ACC_EN, B_EN, comparator_1_eq, comparator_5_eq, decoder_1_out6, decoder_1_out7, decoder_1_out8,
       decoder_1_out9, IR_EN, MAR_EN, Mux_B, Mux_MAR, Mux_PC, PC_EN;
  wire [1:0] ALU_C, Mux_ACC;
  wire [3:0] F_CU;
  wire [10:0] adder_1_out, ADDR_CU, IR_ADDR, multiplexer_1_out, multiplexer_2_out, PC_q;
  wire [21:0] ALU_OUT, B_OUT, BOOTH, multiplexer_3_out, multiplexer_4_out;
  wire [21:11] IR_q;

  Adder #(.width(11)) adder_1 (.a(PC_q), .b(11'h1), .out(adder_1_out), .cin(1'b0));  // open: cout
  // NOT_Gate not_1 is placed but not wired
  Register #(.width(22)) IR (.D(B_OUT), .en(IR_EN), .Q({IR_q, IR_ADDR}), .clk(clock), .clr(1'b0));
  Multiplexer #(.width(11), .enable("false")) multiplexer_1 (
    .in0(adder_1_out), .in1(IR_ADDR), .out(multiplexer_1_out), .sel(Mux_PC));
  Register #(.width(11), .trigger("falling")) PC (
    .D(multiplexer_1_out), .en(PC_EN), .Q(PC_q), .clk(clock), .clr(Reset));
  // Probe on F_CU
  CU cu_1 (
    .reset(Reset), .Opcode_In(IR_q[21:17]), .AD(ADDR_CU), .F(F_CU), .Mem_RD(MemRead), .Mem_WR(MemWrite),
    .HLT(HLT), .clock(clock));
  Multiplexer #(.width(11), .enable("false")) multiplexer_2 (
    .in0(PC_q), .in1(IR_ADDR), .out(multiplexer_2_out), .sel(Mux_MAR));
  ALU_22 alu_22_1 ();
  Register #(.width(11), .trigger("falling")) MAR (
    .D(multiplexer_2_out), .en(MAR_EN), .Q(MemAddress), .clk(clock), .clr(1'b0));
  Multiplexer #(.width(22), .enable("false")) multiplexer_3 (
    .in0(Mem_DataIN), .in1(Mem_DataOut), .out(multiplexer_3_out), .sel(Mux_B));
  Register #(.width(22)) B (.D(multiplexer_3_out), .en(B_EN), .Q(B_OUT), .clk(clock), .clr(1'b0));
  Decoder #(.select(4), .enable("false")) decoder_1 (
    .out6(decoder_1_out6), .out7(decoder_1_out7), .out8(decoder_1_out8), .out9(decoder_1_out9),
    .out12(Mux_ACC[0]), .out13(Mux_ACC[1]), .sel(F_CU));  // open: out0, out1, out2, out3, out4, out5, out10, out11, out14, out15
  _22_bit_ALU_main main_1 (
    .Control(ALU_C), .A(Mem_DataOut), .B(B_OUT), .Result(ALU_OUT));  // open: Zero, Negative, Overflow, Carry
  or cb1 (ALU_C[1], decoder_1_out7, decoder_1_out9);
  or cb0 (ALU_C[0], decoder_1_out8, decoder_1_out9);
  Multiplexer #(.select(2), .width(22), .enable("false")) multiplexer_4 (
    .in0(ALU_OUT), .in1(B_OUT), .in2(BOOTH), .out(multiplexer_4_out), .sel(Mux_ACC));  // open: in3
  or or_1 (ACC_EN, decoder_1_out6, decoder_1_out7, decoder_1_out8, decoder_1_out9, Mux_ACC[0], Mux_ACC[1]);
  Register #(.width(22), .trigger("falling")) A_ACC (
    .D(multiplexer_4_out), .en(ACC_EN), .Q(Mem_DataOut), .clk(clock), .clr(Reset));
  Comparator #(.width(4)) comparator_1 (.a(F_CU), .b(4'b0001), .eq(comparator_1_eq));  // open: gt, lt
  Comparator #(.width(4)) comparator_2 (.a(F_CU), .b(4'b0101), .eq(Mux_MAR));  // open: gt, lt
  Comparator #(.width(4)) comparator_3 (.a(F_CU), .b(4'b0011), .eq(IR_EN));  // open: gt, lt
  Comparator #(.width(4)) comparator_4 (.a(F_CU), .b(4'b1010), .eq(Mux_B));  // open: gt, lt
  Comparator #(.width(4)) comparator_5 (.a(F_CU), .b(4'b0010), .eq(comparator_5_eq));  // open: gt, lt
  Comparator #(.width(4)) comparator_6 (.a(F_CU), .b(4'b0100), .eq(Mux_PC));  // open: gt, lt
  or or_2 (MAR_EN, comparator_1_eq, Mux_MAR);
  or or_3 (B_EN, IR_EN, Mux_B);
  or or_4 (PC_EN, comparator_5_eq, Mux_PC);

  // Other names for the same wires on the sheet: A_OUT[21:0] = Mem_DataOut; CLK = clock; CLR = Reset
endmodule
